# Fritzing sketch Wireing Barto (saved by Fritzing 0.9.3b)

parts:
  WATER_PUMP = water pump/motor
  A4 = 2-Channel 5v Relay Shield [package=relay-2ch5v10a]
  LCD_I2C = LCD1602-I2C
  Stepdown_5V = LM2596 step down module
  Power_Supply_12v = prefix0000 [part_number=S-350-60]
  SENSOR_PH1 = ph-4502c [package=THT]
  WATER_VALVE = Plastic Solenoid Valve
  U1 = ESP32-38PinWide [part_number=ESP32-38PinWide]
  Water_Level_Sensor = Water Level Sensor
  DSB1820 = DS18B20 1-Wire Temperature Sensor Probe

nets:
  GND: WATER_PUMP.pin_1, A4.Pin_10, LCD_I2C.GND, Stepdown_5V.IN-, Stepdown_5V.OUT-, Power_Supply_12v.connector3, SENSOR_PH1.pin4, SENSOR_PH1.pin5, WATER_VALVE.no_name_yet#2, U1.GND, Water_Level_Sensor.GND, DSB1820.GND
  N1: WATER_PUMP.pin_2, A4.Pin_2
  N2: A4.Pin_1, A4.Pin_4, Stepdown_5V.IN+, Power_Supply_12v.connector0
  N3: A4.Pin_5, WATER_VALVE.no_name_yet#1
  N4: A4.Pin_11, U1.GPIO17
  N5: A4.Pin_12, U1.GPIO16
  VCC: A4.Pin_13, LCD_I2C.VCC, Stepdown_5V.OUT+, U1.VIN
  N6: LCD_I2C.SDA, U1.GPIO21
  N7: LCD_I2C.SCL, U1.GPIO22
  N8: SENSOR_PH1.pin3, U1.GPIO34
  VCC_2: SENSOR_PH1.pin6, U1.3.3, Water_Level_Sensor.VCC, DSB1820.VDD
  N9: U1.GPIO4, DSB1820.DQ
  N10: U1.GPIO18, Water_Level_Sensor.SIG

custom parts:
  water pump/motor: WATER PUMP BY ARDUBLOCKTR
  2-Channel 5v Relay Shield: 2 Channel 5v Relay Shield w. 2x SPD-06VDC-SD-C
  LCD1602-I2C: A standard character display, usually with 2x16 characters. Comes in many colors with LCM1602 IIC attached.
  LM2596 step down module: LM2596 DC-DC step down power supply module 3 A.
  ph-4502c: ph-4502c PH Meter.
  ESP32-38PinWide: Generic 38-Pin ESP32 with wide format (only access to one side of pins on a breadboard) based on Stephen Lilley's HiLetgo ESP-WROOM-32 ESP32 ESP-32S Development Board.
  Water Level Sensor: A water level sensor. This sensor operates at 3V to 5V. The Sig (signal) pin outputs an analogue signal that is in proportion to the amount of water in contact with the sensor.
